// Logisim project cirq01.circ as structural Verilog: 2 circuits, main circuit collatz_stepper
module collatz_stepper (
  input  [7:0] Input_Number,
  output [7:0] One_Step_Collatz,
  output [7:0] out_3,
  output [7:0] out_4,
  output [7:0] out_5
);

  wire [7:0] shifter_1_out;

  Shifter #(.shift("lr")) shifter_1 (.in(Input_Number), .\dist (3'b001), .out(shifter_1_out));
  Shifter shifter_2 (.in(Input_Number), .\dist (3'b001), .out(out_3));
  Adder adder_1 (.a(out_3), .b(Input_Number), .out(out_4), .cin(1'b1));  // open: cout
  Multiplexer #(.width(8)) multiplexer_1 (
    .in0(shifter_1_out), .in1(out_4), .out(One_Step_Collatz), .sel(Input_Number[0]));

  assign out_5 = Input_Number;
endmodule

module buttoned (
  input  [7:0] in_1,
  output [7:0] out_2,
  output [7:0] out_3
);

  wire nor_1_out, Reset_out, Step_out;
  wire [7:0] multiplexer_1_out;

  Button Step (.out(Step_out));
  Button Reset (.out(Reset_out));
  Multiplexer #(.width(8)) multiplexer_1 (.in0(out_2), .in1(in_1), .out(multiplexer_1_out), .sel(nor_1_out));
  nor nor_1 (nor_1_out, out_3[0], out_3[1], out_3[2], out_3[3], out_3[4], out_3[5], out_3[6], out_3[7]);
  Register register_1 (.D(multiplexer_1_out), .en(1'b1), .clk(Step_out), .Q(out_3), .clr(Reset_out));
  Hex_Digit_Display hex_digit_display_1 (.value(out_2[7:4]));  // open: dp
  collatz_stepper collatz_stepper_1 (.Input_Number(out_3), .One_Step_Collatz(out_2));  // open: out_3, out_4, out_5
  Hex_Digit_Display hex_digit_display_2 (.value(out_2[3:0]));  // open: dp
endmodule
