// Logisim project collatz_orbit_unit_16bit.circ as structural Verilog: 2 circuits, main circuit COU
module COU (
  input  Reset,
  input  [15:0] Data_In,
  input  Start,
  input  Clock,
  output Have_Result,
  output Overflow,
  output [15:0] Orbit_Length,
  output [15:0] Path_Record
);

  wire and_1_out, and_2_out, d_ff_1_q, nor_1_out, not_1_out, not_2_out, not_3_out, or_1_out,
       subtractor_1_bout;
  wire [15:0] adder_1_out, Iterator_q, multiplexer_1_out, multiplexer_2_out, shifter_1_out, shifter_2_out,
       Tmp_Buf_q;

  Multiplexer #(.width(16)) multiplexer_1 (.in0(Tmp_Buf_q), .in1(Data_In), .out(multiplexer_1_out), .sel(Start));
  and and_1 (and_1_out, Clock, not_3_out);
  Register #(.trigger("high"), .width(16)) Iterator (
    .D(multiplexer_1_out), .en(or_1_out), .clk(or_1_out), .Q(Iterator_q), .clr(Reset));
  or or_1 (or_1_out, d_ff_1_q, Start);
  not not_1 (not_1_out, d_ff_1_q);
  D_Flip_Flop d_ff_1 (.D(not_1_out), .clk(not_2_out), .Q(d_ff_1_q), .reset(Reset));  // open: Qn, preset
  not not_2 (not_2_out, and_1_out);
  Counter #(.max('hffff), .width(16)) counter_1 (
    .clr(Reset), .load(1'b0), .up(1'b1), .count(not_3_out), .clk(Clock), .D({16{1'b0}}), .Q(Orbit_Length));  // open: carry
  Register #(.width(16)) Path_Record_Reg (.D(Tmp_Buf_q), .en(and_2_out), .clk(and_2_out), .Q(Path_Record), .clr(Reset));
  and and_2 (and_2_out, d_ff_1_q, subtractor_1_bout);
  Shifter #(.width(16)) shifter_1 (.in(Iterator_q), .\dist (4'b0001), .out(shifter_1_out));
  not not_3 (not_3_out, Have_Result);
  Shifter #(.shift("lr"), .width(16)) shifter_2 (.in(Iterator_q), .\dist (4'b0001), .out(shifter_2_out));
  Adder #(.width(16)) adder_1 (.a(Iterator_q), .b(shifter_1_out), .out(adder_1_out), .cin(1'b1), .cout(Overflow));
  Subtractor #(.width(16)) subtractor_1 (
    .a(Path_Record), .b(Tmp_Buf_q), .bin(1'b0), .bout(subtractor_1_bout));  // open: out
  Multiplexer #(.width(16)) multiplexer_2 (
    .in0(shifter_2_out), .in1(adder_1_out), .out(multiplexer_2_out), .sel(Iterator_q[0]));
  Register #(.width(16)) Tmp_Buf (.D(multiplexer_2_out), .en(and_1_out), .clk(and_1_out), .Q(Tmp_Buf_q), .clr(Reset));
  and and_3 (Have_Result, Tmp_Buf_q[0], nor_1_out);
  nor nor_1 (nor_1_out, Tmp_Buf_q[1], Tmp_Buf_q[2], Tmp_Buf_q[3], Tmp_Buf_q[4], Tmp_Buf_q[5], Tmp_Buf_q[6], Tmp_Buf_q[7], Tmp_Buf_q[8], Tmp_Buf_q[9], Tmp_Buf_q[10], Tmp_Buf_q[11], Tmp_Buf_q[12], Tmp_Buf_q[13], Tmp_Buf_q[14], Tmp_Buf_q[15]);
endmodule

module main (
);

  wire clock_1_out, cou_1_overflow, cou_2_overflow, cou_3_overflow, cou_4_overflow, cou_5_overflow,
       cou_6_overflow, cou_7_overflow, cou_8_overflow, cou_9_overflow, cou_10_overflow, cou_11_overflow,
       cou_12_overflow, cou_13_overflow, cou_14_overflow, cou_15_overflow, cou_16_overflow, cou_17_overflow,
       cou_18_overflow, cou_19_overflow, cou_20_overflow, cou_21_overflow, cou_22_overflow, cou_23_overflow,
       cou_24_overflow, cou_25_overflow, cou_26_overflow, cou_27_overflow, cou_28_overflow, cou_29_overflow,
       cou_30_overflow, cou_31_overflow, cou_32_overflow, Reset_out, Start_out;
  wire [7:0] cou_8_have_result, cou_16_have_result, cou_24_have_result, cou_32_have_result;
  wire [15:0] cou_1_orbit_length, cou_1_path_record, cou_2_orbit_length, cou_2_path_record,
       cou_3_orbit_length, cou_3_path_record, cou_4_orbit_length, cou_4_path_record, cou_5_orbit_length,
       cou_5_path_record, cou_6_orbit_length, cou_6_path_record, cou_7_orbit_length, cou_7_path_record,
       cou_8_orbit_length, cou_8_path_record, cou_9_orbit_length, cou_9_path_record, cou_10_orbit_length,
       cou_10_path_record, cou_11_orbit_length, cou_11_path_record, cou_12_orbit_length, cou_12_path_record,
       cou_13_orbit_length, cou_13_path_record, cou_14_orbit_length, cou_14_path_record, cou_15_orbit_length,
       cou_15_path_record, cou_16_orbit_length, cou_16_path_record, cou_17_orbit_length, cou_17_path_record,
       cou_18_orbit_length, cou_18_path_record, cou_19_orbit_length, cou_19_path_record, cou_20_orbit_length,
       cou_20_path_record, cou_21_orbit_length, cou_21_path_record, cou_22_orbit_length, cou_22_path_record,
       cou_23_orbit_length, cou_23_path_record, cou_24_orbit_length, cou_24_path_record, cou_25_orbit_length,
       cou_25_path_record, cou_26_orbit_length, cou_26_path_record, cou_27_orbit_length, cou_27_path_record,
       cou_28_orbit_length, cou_28_path_record, cou_29_orbit_length, cou_29_path_record, cou_30_orbit_length,
       cou_30_path_record, cou_31_orbit_length, cou_31_path_record, cou_32_orbit_length, cou_32_path_record;

  Button Reset (.out(Reset_out));
  Button Start (.out(Start_out));
  Clock clock_1 (.out(clock_1_out));
  COU cou_1 (
    .Reset(Reset_out), .Data_In(16'h93), .Start(Start_out), .Clock(clock_1_out),
    .Have_Result(cou_8_have_result[7]), .Overflow(cou_1_overflow), .Orbit_Length(cou_1_orbit_length),
    .Path_Record(cou_1_path_record));
  COU cou_2 (
    .Reset(Reset_out), .Data_In(16'h93), .Start(Start_out), .Clock(clock_1_out),
    .Have_Result(cou_8_have_result[6]), .Overflow(cou_2_overflow), .Orbit_Length(cou_2_orbit_length),
    .Path_Record(cou_2_path_record));
  COU cou_3 (
    .Reset(Reset_out), .Data_In(16'h88), .Start(Start_out), .Clock(clock_1_out),
    .Have_Result(cou_8_have_result[5]), .Overflow(cou_3_overflow), .Orbit_Length(cou_3_orbit_length),
    .Path_Record(cou_3_path_record));
  COU cou_4 (
    .Reset(Reset_out), .Data_In(16'ha10), .Start(Start_out), .Clock(clock_1_out),
    .Have_Result(cou_8_have_result[4]), .Overflow(cou_4_overflow), .Orbit_Length(cou_4_orbit_length),
    .Path_Record(cou_4_path_record));
  COU cou_5 (
    .Reset(Reset_out), .Data_In(16'h93), .Start(Start_out), .Clock(clock_1_out),
    .Have_Result(cou_8_have_result[3]), .Overflow(cou_5_overflow), .Orbit_Length(cou_5_orbit_length),
    .Path_Record(cou_5_path_record));
  COU cou_6 (
    .Reset(Reset_out), .Data_In(16'h93), .Start(Start_out), .Clock(clock_1_out),
    .Have_Result(cou_8_have_result[2]), .Overflow(cou_6_overflow), .Orbit_Length(cou_6_orbit_length),
    .Path_Record(cou_6_path_record));
  COU cou_7 (
    .Reset(Reset_out), .Data_In(16'h88), .Start(Start_out), .Clock(clock_1_out),
    .Have_Result(cou_8_have_result[1]), .Overflow(cou_7_overflow), .Orbit_Length(cou_7_orbit_length),
    .Path_Record(cou_7_path_record));
  COU cou_8 (
    .Reset(Reset_out), .Data_In(16'ha10), .Start(Start_out), .Clock(clock_1_out),
    .Have_Result(cou_8_have_result[0]), .Overflow(cou_8_overflow), .Orbit_Length(cou_8_orbit_length),
    .Path_Record(cou_8_path_record));
  // Probe on cou_8_have_result[7]
  // Probe on cou_1_overflow
  // Probe on cou_1_orbit_length
  // Probe on cou_1_path_record
  // Probe on cou_8_have_result[6]
  // Probe on cou_2_overflow
  // Probe on cou_2_orbit_length
  // Probe on cou_2_path_record
  // Probe on cou_8_have_result[5]
  // Probe on cou_3_overflow
  // Probe on cou_3_orbit_length
  // Probe on cou_3_path_record
  // Probe on cou_8_have_result[4]
  // Probe on cou_4_overflow
  // Probe on cou_4_orbit_length
  // Probe on cou_4_path_record
  // Probe on cou_8_have_result[3]
  // Probe on cou_5_overflow
  // Probe on cou_5_orbit_length
  // Probe on cou_5_path_record
  // Probe on cou_8_have_result[2]
  // Probe on cou_6_overflow
  // Probe on cou_6_orbit_length
  // Probe on cou_6_path_record
  // Probe on cou_8_have_result[1]
  // Probe on cou_7_overflow
  // Probe on cou_7_orbit_length
  // Probe on cou_7_path_record
  // Probe on cou_8_have_result[0]
  // Probe on cou_8_overflow
  // Probe on cou_8_orbit_length
  // Probe on cou_8_path_record
  DotMatrix #(.matrixcols(4), .matrixrows(8)) dotmatrix_1 (
    .col0(cou_8_have_result), .col1(cou_16_have_result), .col2(cou_24_have_result), .col3(cou_32_have_result));
  COU cou_9 (
    .Reset(Reset_out), .Data_In(16'hb03), .Start(Start_out), .Clock(clock_1_out),
    .Have_Result(cou_16_have_result[7]), .Overflow(cou_9_overflow), .Orbit_Length(cou_9_orbit_length),
    .Path_Record(cou_9_path_record));
  COU cou_10 (
    .Reset(Reset_out), .Data_In(16'hc7a), .Start(Start_out), .Clock(clock_1_out),
    .Have_Result(cou_16_have_result[6]), .Overflow(cou_10_overflow), .Orbit_Length(cou_10_orbit_length),
    .Path_Record(cou_10_path_record));
  COU cou_11 (
    .Reset(Reset_out), .Data_In(16'h12), .Start(Start_out), .Clock(clock_1_out),
    .Have_Result(cou_16_have_result[5]), .Overflow(cou_11_overflow), .Orbit_Length(cou_11_orbit_length),
    .Path_Record(cou_11_path_record));
  COU cou_12 (
    .Reset(Reset_out), .Data_In(16'h47), .Start(Start_out), .Clock(clock_1_out),
    .Have_Result(cou_16_have_result[4]), .Overflow(cou_12_overflow), .Orbit_Length(cou_12_orbit_length),
    .Path_Record(cou_12_path_record));
  COU cou_13 (
    .Reset(Reset_out), .Data_In(16'hb03), .Start(Start_out), .Clock(clock_1_out),
    .Have_Result(cou_16_have_result[3]), .Overflow(cou_13_overflow), .Orbit_Length(cou_13_orbit_length),
    .Path_Record(cou_13_path_record));
  COU cou_14 (
    .Reset(Reset_out), .Data_In(16'hc7a), .Start(Start_out), .Clock(clock_1_out),
    .Have_Result(cou_16_have_result[2]), .Overflow(cou_14_overflow), .Orbit_Length(cou_14_orbit_length),
    .Path_Record(cou_14_path_record));
  COU cou_15 (
    .Reset(Reset_out), .Data_In(16'h12), .Start(Start_out), .Clock(clock_1_out),
    .Have_Result(cou_16_have_result[1]), .Overflow(cou_15_overflow), .Orbit_Length(cou_15_orbit_length),
    .Path_Record(cou_15_path_record));
  COU cou_16 (
    .Reset(Reset_out), .Data_In(16'h47), .Start(Start_out), .Clock(clock_1_out),
    .Have_Result(cou_16_have_result[0]), .Overflow(cou_16_overflow), .Orbit_Length(cou_16_orbit_length),
    .Path_Record(cou_16_path_record));
  // Probe on cou_16_have_result[7]
  // Probe on cou_9_overflow
  // Probe on cou_9_orbit_length
  // Probe on cou_9_path_record
  // Probe on cou_16_have_result[6]
  // Probe on cou_10_overflow
  // Probe on cou_10_orbit_length
  // Probe on cou_10_path_record
  // Probe on cou_16_have_result[5]
  // Probe on cou_11_overflow
  // Probe on cou_11_orbit_length
  // Probe on cou_11_path_record
  // Probe on cou_16_have_result[4]
  // Probe on cou_12_overflow
  // Probe on cou_12_orbit_length
  // Probe on cou_12_path_record
  // Probe on cou_16_have_result[3]
  // Probe on cou_13_overflow
  // Probe on cou_13_orbit_length
  // Probe on cou_13_path_record
  // Probe on cou_16_have_result[2]
  // Probe on cou_14_overflow
  // Probe on cou_14_orbit_length
  // Probe on cou_14_path_record
  // Probe on cou_16_have_result[1]
  // Probe on cou_15_overflow
  // Probe on cou_15_orbit_length
  // Probe on cou_15_path_record
  // Probe on cou_16_have_result[0]
  // Probe on cou_16_overflow
  // Probe on cou_16_orbit_length
  // Probe on cou_16_path_record
  COU cou_17 (
    .Reset(Reset_out), .Data_In(16'h93), .Start(Start_out), .Clock(clock_1_out),
    .Have_Result(cou_24_have_result[7]), .Overflow(cou_17_overflow), .Orbit_Length(cou_17_orbit_length),
    .Path_Record(cou_17_path_record));
  COU cou_18 (
    .Reset(Reset_out), .Data_In(16'h93), .Start(Start_out), .Clock(clock_1_out),
    .Have_Result(cou_24_have_result[6]), .Overflow(cou_18_overflow), .Orbit_Length(cou_18_orbit_length),
    .Path_Record(cou_18_path_record));
  COU cou_19 (
    .Reset(Reset_out), .Data_In(16'h88), .Start(Start_out), .Clock(clock_1_out),
    .Have_Result(cou_24_have_result[5]), .Overflow(cou_19_overflow), .Orbit_Length(cou_19_orbit_length),
    .Path_Record(cou_19_path_record));
  COU cou_20 (
    .Reset(Reset_out), .Data_In(16'ha10), .Start(Start_out), .Clock(clock_1_out),
    .Have_Result(cou_24_have_result[4]), .Overflow(cou_20_overflow), .Orbit_Length(cou_20_orbit_length),
    .Path_Record(cou_20_path_record));
  COU cou_21 (
    .Reset(Reset_out), .Data_In(16'h93), .Start(Start_out), .Clock(clock_1_out),
    .Have_Result(cou_24_have_result[3]), .Overflow(cou_21_overflow), .Orbit_Length(cou_21_orbit_length),
    .Path_Record(cou_21_path_record));
  COU cou_22 (
    .Reset(Reset_out), .Data_In(16'h93), .Start(Start_out), .Clock(clock_1_out),
    .Have_Result(cou_24_have_result[2]), .Overflow(cou_22_overflow), .Orbit_Length(cou_22_orbit_length),
    .Path_Record(cou_22_path_record));
  COU cou_23 (
    .Reset(Reset_out), .Data_In(16'h88), .Start(Start_out), .Clock(clock_1_out),
    .Have_Result(cou_24_have_result[1]), .Overflow(cou_23_overflow), .Orbit_Length(cou_23_orbit_length),
    .Path_Record(cou_23_path_record));
  COU cou_24 (
    .Reset(Reset_out), .Data_In(16'ha10), .Start(Start_out), .Clock(clock_1_out),
    .Have_Result(cou_24_have_result[0]), .Overflow(cou_24_overflow), .Orbit_Length(cou_24_orbit_length),
    .Path_Record(cou_24_path_record));
  // Probe on cou_24_have_result[7]
  // Probe on cou_17_overflow
  // Probe on cou_17_orbit_length
  // Probe on cou_17_path_record
  // Probe on cou_24_have_result[6]
  // Probe on cou_18_overflow
  // Probe on cou_18_orbit_length
  // Probe on cou_18_path_record
  // Probe on cou_24_have_result[5]
  // Probe on cou_19_overflow
  // Probe on cou_19_orbit_length
  // Probe on cou_19_path_record
  // Probe on cou_24_have_result[4]
  // Probe on cou_20_overflow
  // Probe on cou_20_orbit_length
  // Probe on cou_20_path_record
  // Probe on cou_24_have_result[3]
  // Probe on cou_21_overflow
  // Probe on cou_21_orbit_length
  // Probe on cou_21_path_record
  // Probe on cou_24_have_result[2]
  // Probe on cou_22_overflow
  // Probe on cou_22_orbit_length
  // Probe on cou_22_path_record
  // Probe on cou_24_have_result[1]
  // Probe on cou_23_overflow
  // Probe on cou_23_orbit_length
  // Probe on cou_23_path_record
  // Probe on cou_24_have_result[0]
  // Probe on cou_24_overflow
  // Probe on cou_24_orbit_length
  // Probe on cou_24_path_record
  COU cou_25 (
    .Reset(Reset_out), .Data_In(16'hb03), .Start(Start_out), .Clock(clock_1_out),
    .Have_Result(cou_32_have_result[7]), .Overflow(cou_25_overflow), .Orbit_Length(cou_25_orbit_length),
    .Path_Record(cou_25_path_record));
  COU cou_26 (
    .Reset(Reset_out), .Data_In(16'hc7a), .Start(Start_out), .Clock(clock_1_out),
    .Have_Result(cou_32_have_result[6]), .Overflow(cou_26_overflow), .Orbit_Length(cou_26_orbit_length),
    .Path_Record(cou_26_path_record));
  COU cou_27 (
    .Reset(Reset_out), .Data_In(16'h12), .Start(Start_out), .Clock(clock_1_out),
    .Have_Result(cou_32_have_result[5]), .Overflow(cou_27_overflow), .Orbit_Length(cou_27_orbit_length),
    .Path_Record(cou_27_path_record));
  COU cou_28 (
    .Reset(Reset_out), .Data_In(16'h47), .Start(Start_out), .Clock(clock_1_out),
    .Have_Result(cou_32_have_result[4]), .Overflow(cou_28_overflow), .Orbit_Length(cou_28_orbit_length),
    .Path_Record(cou_28_path_record));
  COU cou_29 (
    .Reset(Reset_out), .Data_In(16'hb03), .Start(Start_out), .Clock(clock_1_out),
    .Have_Result(cou_32_have_result[3]), .Overflow(cou_29_overflow), .Orbit_Length(cou_29_orbit_length),
    .Path_Record(cou_29_path_record));
  COU cou_30 (
    .Reset(Reset_out), .Data_In(16'hc7a), .Start(Start_out), .Clock(clock_1_out),
    .Have_Result(cou_32_have_result[2]), .Overflow(cou_30_overflow), .Orbit_Length(cou_30_orbit_length),
    .Path_Record(cou_30_path_record));
  COU cou_31 (
    .Reset(Reset_out), .Data_In(16'h12), .Start(Start_out), .Clock(clock_1_out),
    .Have_Result(cou_32_have_result[1]), .Overflow(cou_31_overflow), .Orbit_Length(cou_31_orbit_length),
    .Path_Record(cou_31_path_record));
  COU cou_32 (
    .Reset(Reset_out), .Data_In(16'h47), .Start(Start_out), .Clock(clock_1_out),
    .Have_Result(cou_32_have_result[0]), .Overflow(cou_32_overflow), .Orbit_Length(cou_32_orbit_length),
    .Path_Record(cou_32_path_record));
  // Probe on cou_32_have_result[7]
  // Probe on cou_25_overflow
  // Probe on cou_25_orbit_length
  // Probe on cou_25_path_record
  // Probe on cou_32_have_result[6]
  // Probe on cou_26_overflow
  // Probe on cou_26_orbit_length
  // Probe on cou_26_path_record
  // Probe on cou_32_have_result[5]
  // Probe on cou_27_overflow
  // Probe on cou_27_orbit_length
  // Probe on cou_27_path_record
  // Probe on cou_32_have_result[4]
  // Probe on cou_28_overflow
  // Probe on cou_28_orbit_length
  // Probe on cou_28_path_record
  // Probe on cou_32_have_result[3]
  // Probe on cou_29_overflow
  // Probe on cou_29_orbit_length
  // Probe on cou_29_path_record
  // Probe on cou_32_have_result[2]
  // Probe on cou_30_overflow
  // Probe on cou_30_orbit_length
  // Probe on cou_30_path_record
  // Probe on cou_32_have_result[1]
  // Probe on cou_31_overflow
  // Probe on cou_31_orbit_length
  // Probe on cou_31_path_record
  // Probe on cou_32_have_result[0]
  // Probe on cou_32_overflow
  // Probe on cou_32_orbit_length
  // Probe on cou_32_path_record
endmodule
